# Fritzing sketch wiring (saved by Fritzing 0.9.3b)

parts:
  R3 = Resistor [tolerance=±5% resistance=4.7k package=THT]
  KY-1 = Keyes Relay [part_number=Relay package=THT]
  DS18B20 = DS18B20 1-Wire Temperature Sensor [part_number=.]
  ProMini_5V = Arduino Pro Mini (5V)
  DC_Output = Power Jack [package=power_jack_combo]
  DC_Input = Power Jack [package=power_jack_combo]

nets:
  VDD: R3.Pin_0, KY-1.power, DS18B20.VDD, ProMini_5V.VCC
  N1: R3.Pin_1, DS18B20.DQ, ProMini_5V.D3
  N2: KY-1.signal, ProMini_5V.D5
  GND: KY-1.ground, DS18B20.GND, ProMini_5V.GND, DC_Output.GND, DC_Input.GND
  N3: ProMini_5V.RAW, DC_Input.PWR

custom parts:
  Keyes Relay: The Keyes 5V relay module is suitable for SCM development, home appliance control. It uses a 5V~12V TIL control signal which can control DC / AC signal.
